# Fritzing sketch car hardware (saved by Fritzing 0.9.1b)
breadboards: 1

parts:
  Part1 = Arduino Pro Mini v13
  LED1 = smd LED [color="Red (633nm)" package="0805 [SMD]"]
  Parking_LED = smd LED [color="Red (633nm)" package="0805 [SMD]"]
  Parking_LEd = smd LED [color="Red (633nm)" package="0805 [SMD]"]
  LED5 = Gus the Green LED
  LED6 = Gus the Green LED
  Motor_Left/Right = DC Motor
  Motor_Forward/Back = DC Motor
  sonar_front = HC-SR04 Ultrasonic Rangemeter
  Sonar_back = HC-SR04 Ultrasonic Rangemeter
  Part4 = Bluetooth HC-05 Macho
  Rechargable_battery_(4X_1_2_Ni-Cad) = 4 x AAA Battery Mount
  LDR = Photocell (LDR) [package=THT]
  R2 = Resistor [tolerance=±5% resistance=220 package=THT]
  R3 = Resistor [tolerance=±5% resistance=220 package=THT]
  R4 = Resistor [tolerance=±5% resistance=220 package=THT]
  R5 = Resistor [tolerance=±5% resistance=220 package=THT]  # not connected
  R6 = Resistor [tolerance=±5% resistance=220 package=THT]
  R7 = Resistor [tolerance=±5% resistance=220 package=THT]
  Charger = USB LiPoly Charger
  Main_battery_switch = SPST Switch [package=switch-spdt]
  LED2 = smd LED [color="Red (633nm)" package="0805 [SMD]"]  # not connected
  IC2 = L293D [package=THT]
  VCC1 = Battery
  R8 = Resistor [tolerance=±5% resistance=220 package=THT]

nets:
  N1: Part1.A4, Part1.A3
  VCC: Part1.A5, Part1.VCC, sonar_front.VCC, Sonar_back.VCC, Part4.VCC, Rechargable_battery_(4X_1_2_Ni-Cad).+, LDR.pin_1, Charger.VBAT, IC2.Enable_1, IC2.Enable_2, IC2.+V, VCC1.-
  GND: Part1.GND, LED1.anode, sonar_front.GND, Sonar_back.GND, Part4.GND, Main_battery_switch.O, IC2.0V, R8.Pin_0
  N2: Part1.A1, R2.Pin_1, R3.Pin_1
  N3: Part1.A0, LDR.pin_0, R8.Pin_1
  N4: Part1.D13/SCK, IC2.In_4
  N5: Part1.D12/MISO, IC2.In_3
  N6: Part1.D11_PWM/MOSI, IC2.In_2
  N7: Part1.D10_PWM/SS, IC2.In_1
  N8: Part1.D8, R4.Pin_1
  N9: Part1.D7, R6.Pin_1
  N10: Part1.D6_PWM, R7.Pin_1
  N11: Part1.D5_PWM, Sonar_back.Echo
  N12: Part1.D4, Sonar_back.Trig
  N13: Part1.D3_PWM, sonar_front.Echo
  N14: Part1.D2, sonar_front.Trig
  N15: Part1.D1/RX, Part4.TXD
  N16: Part1.D0/TX, Part4.RXD
  N17: Parking_LED.cathode, LED6.cathode
  N18: Parking_LEd.cathode, LED5.cathode
  N19: Motor_Left/Right.pin_1, IC2.Out_2_(_Controlled_by_Enable_1_)
  N20: Motor_Left/Right.pin_2, IC2.Out_1_(_Controlled_by_Enable_1_)
  N21: Motor_Forward/Back.pin_1, IC2.Out_3_(_Controlled_by_Enable_2_)
  N22: Motor_Forward/Back.pin_2, IC2.Out_4_(_Controlled_by_Enable_2_)
  N23: Rechargable_battery_(4X_1_2_Ni-Cad).-, Charger.GND, Main_battery_switch.S
  N24: IC2.+Vmotor, VCC1.+
